# Fritzing sketch fritzing-Sketch (saved by Fritzing 0.9.4)
breadboards: 1

parts:
  DHT1 = DHT22 Humidity and Temperature Sensor
  U1 = NodeMCU V3.0
  Grove1 = Grove OLED 128x96

nets:
  VDD: DHT1.VDD, U1.3V3, Grove1.VCC
  N1: DHT1.DATA, U1.D5
  GND: DHT1.GND, U1.GND#6, U1.GND#13, U1.GND#16, U1.GND#33, Grove1.GND
  N2: U1.D1, Grove1.SCL
  N3: U1.D2, Grove1.SDA

notes:
  Nikos Tsirimiagos

custom parts:
  NodeMCU V3.0: ESP8266 based NodeMCU
